# Fritzing sketch Esp01_Portão (saved by Fritzing 0.9.3b)
circuit board: 3.83436cm x 2.54797cm
breadboards: 1

parts:
  U1 = ESP8266 WiFi Module [part_number=ESP8266]
  J1 = Screw terminal - 2 pins [package=THT]
  R3 = Resistor [tolerance=±5% resistance=3.3k package=THT]
  R2 = Resistor [tolerance=±5% resistance=3.3k package=THT]
  R4 = Resistor [tolerance=±5% resistance=3.3k package=THT]
  R1 = Resistor [tolerance=±5% resistance=3.3k package=THT]
  J2 = Screw terminal - 2 pins [package=THT]
  R5 = Resistor [tolerance=±5% resistance=10k package=THT]
  Q1 = PNP-Transistor [package="TO92 [THT]"]

nets:
  N1: U1.VCC, R3.Pin_1, R2.Pin_1, R4.Pin_1, R1.Pin_1, Q1.E
  N2: U1.GPIO_0, R4.Pin_0
  N3: U1.RST, R3.Pin_0
  N4: U1.GPIO_2, R1.Pin_0
  N5: U1.CH_PD, R2.Pin_0
  N6: U1.GND, J1.pin1, R5.Pin_1
  N7: J1.pin2, J2.pin2, Q1.C
  N8: J2.pin1, R5.Pin_0, Q1.B

custom parts:
  ESP8266 WiFi Module: Generic WiFi Module based on the ESP8266 with onboard PCB antenna and UART communications
