# Fritzing sketch doorsensor_w_regulator (saved by Fritzing 0.9.3b)
circuit board: 4.75965cm x 5.54892cm
breadboards: 1

parts:
  Q1 = PNP-Transistor [package="TO92 [THT]"]
  U1 = ESP8266 WiFi Module [part_number=ESP8266]
  R1 = Resistor [tolerance=±5% resistance=1k package=THT]
  R4 = Resistor [tolerance=±5% resistance=1k package=THT]
  R5 = Resistor [tolerance=±5% resistance=10k package=THT]
  R6 = Resistor [tolerance=±5% resistance=10k package=THT]
  R7 = Resistor [tolerance=±5% resistance=1k package=THT]
  J1 = Screw terminal - 2 pins [package=THT]
  D1 = Schottky Diode [part_number=1N5817 package="300 mil [THT]"]
  IC1 = V_REG_LD1117VXX [package=78xxl]
  J2 = Screw terminal - 2 pins [package=THT]
  C1 = Electrolytic Capacitor [capacitance=10µF package="1010 [SMD, electrolytic]"]
  C2 = Electrolytic Capacitor [capacitance=10µF package="1010 [SMD, electrolytic]"]

nets:
  N1: Q1.E, U1.VCC, J1.pin2, IC1.OUT, C1.+
  N2: Q1.B, R5.Pin_0, J1.pin1
  N3: Q1.C, U1.GPIO_2, R7.Pin_0, D1.anode
  N4: U1.GPIO_0, R1.Pin_0
  N5: U1.CH_PD, R4.Pin_0
  GND: U1.GND, R5.Pin_1, R6.Pin_0, R7.Pin_1, IC1.GND, J2.pin1, C1.-, C2.-
  N6: R1.Pin_1, R4.Pin_1, R6.Pin_1, D1.cathode
  N7: IC1.IN, J2.pin2, C2.+

custom parts:
  ESP8266 WiFi Module: Generic WiFi Module based on the ESP8266 with onboard PCB antenna and UART communications
